// Logisim project MIPS_Processor.circ as structural Verilog: 7 circuits, main circuit main
module main (
  input  RST,
  output [7:0] jump_address,
  output [7:0] out_3,
  output [7:0] PC,
  output [3:0] t0,
  output [3:0] t1,
  output [3:0] t2,
  output [3:0] t3,
  output [3:0] t4,
  output [3:0] sp
);

  wire alu_1_is_zero, and_1_out, CLK_out, control_1_alusrc, control_1_branch, control_1_branchne,
       control_1_jump, control_1_memread, control_1_memtoreg, control_1_memwrite, control_1_regdst,
       control_1_regwrite, xor_1_out;
  wire [2:0] control_1_aluop;
  wire [3:0] alu_1_result, instruction_memory_1_instruction, mem_1_read_data, multiplexer_1_out,
       multiplexer_2_out, multiplexer_3_out, register_file_1_readdata1, register_file_1_readdata2;
  wire [15:12] instruction_memory_1_instruction_2;

  PC_Module pc_module_1 (
    .PC_register_enable(1'b1), .CLK_PC(CLK_out), .PC_register_reset(RST), .jump_address(jump_address),
    .branch_offset(instruction_memory_1_instruction), .jumpControl(control_1_jump), .branchTaken(and_1_out),
    .currentPC(PC), .branch_add(out_3));
  Clock CLK (.out(CLK_out));
  Instruction_Memory instruction_memory_1 (
    .currentPC(PC),
    .instruction({instruction_memory_1_instruction_2, jump_address, instruction_memory_1_instruction}));
  Multiplexer #(.width(4)) multiplexer_1 (
    .in0(jump_address[3:0]), .in1(instruction_memory_1_instruction), .out(multiplexer_1_out),
    .sel(control_1_regdst));
  CONTROL control_1 (
    .Opcode(instruction_memory_1_instruction_2), .ALUOp(control_1_aluop), .Jump(control_1_jump),
    .BranchNE(control_1_branchne), .Branch(control_1_branch), .MemToReg(control_1_memtoreg),
    .MemWrite(control_1_memwrite), .MemRead(control_1_memread), .ALUSrc(control_1_alusrc),
    .RegWrite(control_1_regwrite), .RegDst(control_1_regdst));
  Register_File register_file_1 (
    .CLK_Reg(CLK_out), .Register_Reset(RST), .WriteData(multiplexer_3_out), .ReadReg1(jump_address[7:4]),
    .RegWriteControl(control_1_regwrite), .WriteReg(multiplexer_1_out), .ReadReg2(jump_address[3:0]),
    .ReadData1(register_file_1_readdata1), .ReadData2(register_file_1_readdata2), .t0_OUT(t0), .t1_OUT(t1),
    .t2_OUT(t2), .t3_OUT(t3), .t4_OUT(t4), .sp_OUT(sp));
  Multiplexer #(.width(4)) multiplexer_2 (
    .in0(register_file_1_readdata2), .in1(instruction_memory_1_instruction), .out(multiplexer_2_out),
    .sel(control_1_alusrc));
  ALU alu_1 (
    .A(register_file_1_readdata1), .shamt(instruction_memory_1_instruction), .B(multiplexer_2_out),
    .control(control_1_aluop), .Is_Zero(alu_1_is_zero), .result(alu_1_result));
  xor xor_1 (xor_1_out, control_1_branchne, alu_1_is_zero);
  and and_1 (and_1_out, xor_1_out, control_1_branch);
  MEM mem_1 (
    .MEM_READ(control_1_memread), .MEM_WRITE(control_1_memwrite), .CLK(CLK_out), .ALU_RESULT(alu_1_result),
    .WRITE_DATA(register_file_1_readdata2), .READ_DATA(mem_1_read_data));
  Multiplexer #(.width(4)) multiplexer_3 (
    .in0(alu_1_result), .in1(mem_1_read_data), .out(multiplexer_3_out), .sel(control_1_memtoreg));

  // Notes on the sheet:
  //   WRITE BACK
endmodule

module PC_Module (
  input  PC_register_enable,
  input  CLK_PC,
  input  PC_register_reset,
  input  [7:0] jump_address,
  input  [3:0] branch_offset,
  input  jumpControl,
  input  branchTaken,
  output [7:0] currentPC,
  output [7:0] branch_add
);

  wire [7:0] adder_1_out, bit_extender_1_out, multiplexer_1_out, multiplexer_2_out;

  Register PC_Register (
    .D(multiplexer_2_out), .en(PC_register_enable), .clk(CLK_PC), .Q(currentPC), .clr(PC_register_reset));
  assign bit_extender_1_out = {{4{branch_offset[3]}}, branch_offset};  // Bit_Extender bit_extender_1
  Adder adder_1 (.a(currentPC), .b({8{1'b0}}), .out(adder_1_out), .cin(1'b1));  // open: cout
  Adder adder_2 (.a(currentPC), .b(bit_extender_1_out), .out(branch_add), .cin(1'b0));  // open: cout
  Multiplexer #(.width(8)) multiplexer_1 (
    .in0(adder_1_out), .in1(branch_add), .out(multiplexer_1_out), .sel(branchTaken));
  Multiplexer #(.width(8)) multiplexer_2 (
    .in0(multiplexer_1_out), .in1(jump_address), .out(multiplexer_2_out), .sel(jumpControl));

  // Notes on the sheet:
  //   PC_register_enable: initial=0x1
  //   branch_offset_sign_extension
  //   PC Module
  //   PC + 1
  //   PC + 1 + branch_offset
endmodule

module Instruction_Memory (
  input  [7:0] currentPC,
  output [15:0] instruction
);

  ROM #(.dataWidth(16)) Instruction_Memory (.addr(currentPC), .data(instruction));

  // Notes on the sheet:
  //   PC
  //   contents of Instruction_Memory (hex, n*v repeats v):
  //   d06f d021 d033 4231 4134 4125 a323 f222 2122 61a0 3415 c441 1441 7323 5241 8452 6190 a610 a62f e114
  //   761f b330 7630 9333 61a0 138
endmodule

module Register_File (
  input  CLK_Reg,
  input  Register_Reset,
  input  [3:0] WriteData,
  input  [3:0] ReadReg1,
  input  RegWriteControl,
  input  [3:0] WriteReg,
  input  [3:0] ReadReg2,
  output [3:0] ReadData1,
  output [3:0] ReadData2,
  output [3:0] t0_OUT,
  output [3:0] t1_OUT,
  output [3:0] t2_OUT,
  output [3:0] t3_OUT,
  output [3:0] t4_OUT,
  output [3:0] sp_OUT
);

  wire demultiplexer_1_out0, demultiplexer_1_out1, demultiplexer_1_out2, demultiplexer_1_out3,
       demultiplexer_1_out4, demultiplexer_1_out5, demultiplexer_1_out6;
  wire [3:0] zero_q;

  Demultiplexer #(.enable("true"), .select(4)) demultiplexer_1 (
    .out0(demultiplexer_1_out0), .out1(demultiplexer_1_out1), .out2(demultiplexer_1_out2),
    .out3(demultiplexer_1_out3), .out4(demultiplexer_1_out4), .out5(demultiplexer_1_out5),
    .out6(demultiplexer_1_out6), .in(1'b1), .sel(WriteReg), .en(RegWriteControl));  // open: out7, out8, out9, out10, out11, out12, out13, out14, out15
  Register #(.width(4)) zero (.D(4'b0000), .en(demultiplexer_1_out0), .clk(CLK_Reg), .Q(zero_q), .clr(Register_Reset));
  Register #(.width(4)) t0 (.D(WriteData), .en(demultiplexer_1_out1), .clk(CLK_Reg), .Q(t0_OUT), .clr(Register_Reset));
  Register #(.width(4)) t1 (.D(WriteData), .en(demultiplexer_1_out2), .clk(CLK_Reg), .Q(t1_OUT), .clr(Register_Reset));
  Register #(.width(4)) t2 (.D(WriteData), .en(demultiplexer_1_out3), .clk(CLK_Reg), .Q(t2_OUT), .clr(Register_Reset));
  Register #(.width(4)) t3 (.D(WriteData), .en(demultiplexer_1_out4), .clk(CLK_Reg), .Q(t3_OUT), .clr(Register_Reset));
  Register #(.width(4)) t4 (.D(WriteData), .en(demultiplexer_1_out5), .clk(CLK_Reg), .Q(t4_OUT), .clr(Register_Reset));
  Register #(.width(4)) sp (.D(WriteData), .en(demultiplexer_1_out6), .clk(CLK_Reg), .Q(sp_OUT), .clr(Register_Reset));
  Multiplexer #(.select(4), .width(4)) multiplexer_1 (
    .in0(zero_q), .in1(t0_OUT), .in2(t1_OUT), .in3(t2_OUT), .in4(t3_OUT), .in5(t4_OUT), .in6(sp_OUT),
    .in7(4'b0000), .in8(4'b0000), .in9(4'b0000), .in10(4'b0000), .in11(4'b0000), .in12(4'b0000),
    .in13(4'b0000), .in14(4'b0000), .in15(4'b0000), .out(ReadData1), .sel(ReadReg1));
  Multiplexer #(.select(4), .width(4)) multiplexer_2 (
    .in0(zero_q), .in1(t0_OUT), .in2(t1_OUT), .in3(t2_OUT), .in4(t3_OUT), .in5(t4_OUT), .in6(sp_OUT),
    .in7(4'b0000), .in8(4'b0000), .in9(4'b0000), .in10(4'b0000), .in11(4'b0000), .in12(4'b0000),
    .in13(4'b0000), .in14(4'b0000), .in15(4'b0000), .out(ReadData2), .sel(ReadReg2));

  // Notes on the sheet:
  //   zero write ignored
  //   Register File
endmodule

module MEM (
  input  MEM_READ,
  input  MEM_WRITE,
  input  CLK,
  input  [3:0] ALU_RESULT,
  input  [3:0] WRITE_DATA,
  output [3:0] READ_DATA
);

  wire [7:0] bit_extender_1_out;

  assign bit_extender_1_out = {{4{ALU_RESULT[3]}}, ALU_RESULT};  // Bit_Extender bit_extender_1
  RAM #(.dataWidth(4), .trigger("falling")) ram_1 (
    .addr(bit_extender_1_out), .we(MEM_WRITE), .oe(MEM_READ), .clk(CLK), .din(WRITE_DATA), .dout(READ_DATA));
endmodule

module ALU (
  input  [3:0] A,
  input  [3:0] shamt,
  input  [3:0] B,
  input  [2:0] control,
  output Is_Zero,
  output [3:0] result
);

  wire [3:0] adder_1_out, and_1_out, bit_extender_1_out, bit_extender_3_out, bit_extender_4_out, nor_1_out,
       or_1_out, xor_1_out;
  wire [15:0] bit_extender_2_out, shifter_1_out, shifter_2_out;

  assign bit_extender_1_out = {{3{control[0]}}, control[0]};  // Bit_Extender bit_extender_1
  assign xor_1_out = bit_extender_1_out ^ B;  // XOR_Gate xor_1, 4 bits wide
  Adder #(.width(4)) adder_1 (.a(A), .b(xor_1_out), .out(adder_1_out), .cin(control[0]));  // open: cout
  assign bit_extender_2_out = {{12{1'b0}}, A};  // Bit_Extender bit_extender_2
  Shifter #(.width(16)) shifter_1 (.in(bit_extender_2_out), .\dist (shamt), .out(shifter_1_out));
  Shifter #(.shift("lr"), .width(16)) shifter_2 (.in(bit_extender_2_out), .\dist (shamt), .out(shifter_2_out));
  assign and_1_out = A & B;  // AND_Gate and_1, 4 bits wide
  assign or_1_out = A | B;  // OR_Gate or_1, 4 bits wide
  assign nor_1_out = ~(A | B);  // NOR_Gate nor_1, 4 bits wide
  Bit_Extender #(.in_width(16), .out_width(4)) bit_extender_3 (.in(shifter_1_out), .out(bit_extender_3_out));
  Bit_Extender #(.in_width(16), .out_width(4)) bit_extender_4 (.in(shifter_2_out), .out(bit_extender_4_out));
  Multiplexer #(.select(3), .width(4)) multiplexer_1 (
    .in0(adder_1_out), .in1(adder_1_out), .in2(and_1_out), .in3(or_1_out), .in4(nor_1_out),
    .in5(bit_extender_3_out), .in6(bit_extender_4_out), .in7(4'b0000), .out(result), .sel(control));
  nor nor_2 (Is_Zero, result[0], result[1], result[2], result[3]);
endmodule

module CONTROL (
  input  [3:0] Opcode,
  output [2:0] ALUOp,
  output Jump,
  output BranchNE,
  output Branch,
  output MemToReg,
  output MemWrite,
  output MemRead,
  output ALUSrc,
  output RegWrite,
  output RegDst
);

  wire [6:3] Control_ROM_data;

  ROM #(.addrWidth(4), .dataWidth(16)) Control_ROM (
    .addr(Opcode),
    .data({RegDst, RegWrite, ALUSrc, MemRead, MemWrite, MemToReg, Branch, BranchNE, Jump, Control_ROM_data, ALUOp}));

  // Notes on the sheet:
  //   contents of Control_ROM (hex, n*v repeats v):
  //   301 6006 201 c001 c000 c002 87 7400 c003 c004 2800 6002 6001 6000 6003 6005
endmodule
