// Logisim project Control_Unit.circ as structural Verilog: 1 circuit, main circuit CONTROL
module CONTROL (
  input  [3:0] Opcode,
  output [2:0] ALUOp,
  output Jump,
  output BranchNE,
  output Branch,
  output MemToReg,
  output MemWrite,
  output MemRead,
  output ALUSrc,
  output RegWrite,
  output RegDst
);

  wire [6:3] Control_ROM_data;

  ROM #(.addrWidth(4), .dataWidth(16)) Control_ROM (
    .addr(Opcode),
    .data({RegDst, RegWrite, ALUSrc, MemRead, MemWrite, MemToReg, Branch, BranchNE, Jump, Control_ROM_data, ALUOp}));

  // Notes on the sheet:
  //   contents of Control_ROM (hex, n*v repeats v):
  //   301 6006 201 c001 c000 c002 87 7400 c003 c004 2800 6002 6001 6000 6003 6005
endmodule
