// Logisim project Instruction_Memory_Unit.circ as structural Verilog: 1 circuit, main circuit Instruction_Memory
module Instruction_Memory (
  input  [7:0] currentPC,
  output [15:0] instruction
);

  ROM #(.dataWidth(16)) Instruction_Memory (.addr(currentPC), .data(instruction));

  // Notes on the sheet:
  //   PC
  //   contents of Instruction_Memory (hex, n*v repeats v):
  //   d06f 4605 d023 c661 a620 c221 20c d011 7620 d661 d030 4313 c221 20d 4301 658 6100
endmodule
