// Logisim project Memory_Unit.circ as structural Verilog: 1 circuit, main circuit MEM
module MEM (
  input  MEM_READ,
  input  MEM_WRITE,
  input  CLK,
  input  [3:0] ALU_RESULT,
  input  [3:0] WRITE_DATA,
  output [3:0] READ_DATA
);

  wire [7:0] bit_extender_1_out;

  assign bit_extender_1_out = {{4{ALU_RESULT[3]}}, ALU_RESULT};  // Bit_Extender bit_extender_1
  RAM #(.dataWidth(4)) ram_1 (
    .addr(bit_extender_1_out), .we(MEM_WRITE), .oe(MEM_READ), .clk(CLK), .din(WRITE_DATA), .dout(READ_DATA));
endmodule
