// Logisim project PC_Unit.circ as structural Verilog: 1 circuit, main circuit PC_Module
module PC_Module (
  input  PC_register_enable,
  input  CLK_PC,
  input  PC_register_reset,
  input  [7:0] jump_address,
  input  [3:0] branch_offset,
  input  jumpControl,
  input  branchTaken,
  output [7:0] currentPC
);

  wire [7:0] adder_1_out, adder_2_out, bit_extender_1_out, multiplexer_1_out, multiplexer_2_out;

  Register PC_Register (
    .D(multiplexer_2_out), .en(PC_register_enable), .clk(CLK_PC), .Q(currentPC), .clr(PC_register_reset));
  assign bit_extender_1_out = {{4{branch_offset[3]}}, branch_offset};  // Bit_Extender bit_extender_1
  Adder adder_1 (.a(currentPC), .b({8{1'b0}}), .out(adder_1_out), .cin(1'b1));  // open: cout
  Adder adder_2 (.a(adder_1_out), .b(bit_extender_1_out), .out(adder_2_out), .cin(1'b0));  // open: cout
  Multiplexer #(.width(8)) multiplexer_1 (
    .in0(adder_1_out), .in1(adder_2_out), .out(multiplexer_1_out), .sel(branchTaken));
  Multiplexer #(.width(8)) multiplexer_2 (
    .in0(multiplexer_1_out), .in1(jump_address), .out(multiplexer_2_out), .sel(jumpControl));

  // Notes on the sheet:
  //   PC_register_enable: initial=0x1
  //   branch_offset_sign_extension
  //   PC Module
  //   PC + 1
  //   PC + 1 + branch_offset
endmodule
