// Logisim project Register_File_Unit.circ as structural Verilog: 1 circuit, main circuit Register_File
module Register_File (
  input  CLK_Reg,
  input  Register_Reset,
  input  [3:0] WriteData,
  input  [3:0] ReadReg1,
  input  RegWriteControl,
  input  [3:0] WriteReg,
  input  [3:0] ReadReg2,
  output [3:0] ReadData1,
  output [3:0] ReadData2,
  output [3:0] t0_OUT,
  output [3:0] t1_OUT,
  output [3:0] t2_OUT,
  output [3:0] t3_OUT,
  output [3:0] t4_OUT,
  output [3:0] sp_OUT
);

  wire demultiplexer_1_out0, demultiplexer_1_out1, demultiplexer_1_out2, demultiplexer_1_out3,
       demultiplexer_1_out4, demultiplexer_1_out5, demultiplexer_1_out6;
  wire [3:0] zero_q;

  Demultiplexer #(.enable("true"), .select(4)) demultiplexer_1 (
    .out0(demultiplexer_1_out0), .out1(demultiplexer_1_out1), .out2(demultiplexer_1_out2),
    .out3(demultiplexer_1_out3), .out4(demultiplexer_1_out4), .out5(demultiplexer_1_out5),
    .out6(demultiplexer_1_out6), .in(1'b1), .sel(WriteReg), .en(RegWriteControl));  // open: out7, out8, out9, out10, out11, out12, out13, out14, out15
  Register #(.width(4)) zero (.D(4'b0000), .en(demultiplexer_1_out0), .clk(CLK_Reg), .Q(zero_q), .clr(Register_Reset));
  Register #(.width(4)) t0 (.D(WriteData), .en(demultiplexer_1_out1), .clk(CLK_Reg), .Q(t0_OUT), .clr(Register_Reset));
  Register #(.width(4)) t1 (.D(WriteData), .en(demultiplexer_1_out2), .clk(CLK_Reg), .Q(t1_OUT), .clr(Register_Reset));
  Register #(.width(4)) t2 (.D(WriteData), .en(demultiplexer_1_out3), .clk(CLK_Reg), .Q(t2_OUT), .clr(Register_Reset));
  Register #(.width(4)) t3 (.D(WriteData), .en(demultiplexer_1_out4), .clk(CLK_Reg), .Q(t3_OUT), .clr(Register_Reset));
  Register #(.width(4)) t4 (.D(WriteData), .en(demultiplexer_1_out5), .clk(CLK_Reg), .Q(t4_OUT), .clr(Register_Reset));
  Register #(.width(4)) sp (.D(WriteData), .en(demultiplexer_1_out6), .clk(CLK_Reg), .Q(sp_OUT), .clr(Register_Reset));
  Multiplexer #(.select(4), .width(4)) multiplexer_1 (
    .in0(zero_q), .in1(t0_OUT), .in2(t1_OUT), .in3(t2_OUT), .in4(t3_OUT), .in5(t4_OUT), .in6(sp_OUT),
    .in7(4'b0000), .in8(4'b0000), .in9(4'b0000), .in10(4'b0000), .in11(4'b0000), .in12(4'b0000),
    .in13(4'b0000), .in14(4'b0000), .in15(4'b0000), .out(ReadData1), .sel(ReadReg1));
  Multiplexer #(.select(4), .width(4)) multiplexer_2 (
    .in0(zero_q), .in1(t0_OUT), .in2(t1_OUT), .in3(t2_OUT), .in4(t3_OUT), .in5(t4_OUT), .in6(sp_OUT),
    .in7(4'b0000), .in8(4'b0000), .in9(4'b0000), .in10(4'b0000), .in11(4'b0000), .in12(4'b0000),
    .in13(4'b0000), .in14(4'b0000), .in15(4'b0000), .out(ReadData2), .sel(ReadReg2));

  // Notes on the sheet:
  //   zero write ignored
  //   Register File
endmodule
