// Logisim project mipsALU.circ as structural Verilog: 1 circuit, main circuit ALU
module ALU (
  input  [3:0] A,
  input  [1:0] shamt,
  input  sub,
  input  [3:0] B,
  input  [2:0] control,
  input  [3:0] constant0
);

  wire nor_2_out, nor_3_out, nor_4_out;
  wire [3:0] adder_1_out, and_1_out, multiplexer_1_out, nor_1_out, or_1_out, shifter_1_out, shifter_2_out,
       xor_1_out;

  xor xor_1 (xor_1_out[0], sub, B[0]);
  xor xor_2 (xor_1_out[2], sub, B[2]);
  xor xor_3 (xor_1_out[1], sub, B[1]);
  xor xor_4 (xor_1_out[3], sub, B[3]);
  Adder #(.width(4)) adder_1 (.a(A), .b(xor_1_out), .out(adder_1_out), .cin(sub));  // open: cout
  Shifter #(.width(4)) shifter_1 (.in(A), .\dist (shamt), .out(shifter_1_out));
  Shifter #(.shift("lr"), .width(4)) shifter_2 (.in(A), .\dist (shamt), .out(shifter_2_out));
  assign and_1_out = A & B;  // AND_Gate and_1, 4 bits wide
  assign or_1_out = A | B;  // OR_Gate or_1, 4 bits wide
  assign nor_1_out = ~(A | B);  // NOR_Gate nor_1, 4 bits wide
  Multiplexer #(.select(3), .width(4)) multiplexer_1 (
    .in0(adder_1_out), .in1(adder_1_out), .in2(and_1_out), .in3(or_1_out), .in4(nor_1_out),
    .in5(shifter_1_out), .in6(shifter_2_out), .in7(constant0), .out(multiplexer_1_out), .sel(control));
  nor nor_2 (nor_2_out, multiplexer_1_out[0], multiplexer_1_out[1]);
  nor nor_3 (nor_3_out, nor_2_out, multiplexer_1_out[2]);
  nor nor_4 (nor_4_out, nor_3_out, multiplexer_1_out[3]);

  // Notes on the sheet:
  //   result
endmodule
